# Fritzing sketch Lab1 (saved by Fritzing 0.9.3b)
breadboards: 1

parts:
  Part1 = Arduino Uno (Rev3)
  LED1 = RGB LED - (4 legs) [package="5 mm [THT]"]
  R1 = Resistor [tolerance=±5% resistance=220 package="0805 [SMD]"]
  R2 = Resistor [tolerance=±5% resistance=220 package="0805 [SMD]"]
  R3 = Resistor [tolerance=±5% resistance=220 package="0805 [SMD]"]
  S1 = Toggle Switch [package=THT]
  R4 = Resistor [tolerance=±5% resistance=220 package=THT]
  R5 = Resistor [tolerance=±5% resistance=220 package=THT]
  LED2 = LED - 5mm [color="Red (633nm)" package="5 mm [THT]"]
  R6 = Resistor [tolerance=±5% resistance=220 package=THT]
  R7 = PHOTOCELL [package=photocell]
  R8 = Resistor [tolerance=±5% resistance=220 package=THT]
  S2 = Pushbutton [package="[THT]"]
  R9 = Resistor [tolerance=±5% resistance=220 package=THT]

nets:
  N1: Part1.A0, R7.P$1
  N2: Part1.D10_PWM/SS, S1.COM, R5.Pin_1
  N3: Part1.D11_PWM/MOSI, R6.Pin_0
  N4: Part1.GND, R5.Pin_0, R8.Pin_0
  N5: Part1.D3_PWM, S2.Pin_1, S2.Pin_2, R9.Pin_0, R9.Pin_1
  N6: Part1.D4, R2.Pin_1
  N7: LED1.red_cathode, R1.Pin_0
  N8: LED1.common_anode, S2.Pin_3, S2.Pin_4
  N9: LED1.green_cathode, R2.Pin_0
  N10: LED1.blue_cathode, R3.Pin_0
  N11: S1.L2, R4.Pin_1
  N12: LED2.cathode, R6.Pin_1
